# Fritzing sketch WaterCap (saved by Fritzing 0.9.3b)
breadboards: 1

parts:
  Part1 = Arduino Uno (Rev3)
  R1 = Resistor [tolerance=±5% resistance=220 package="0603 [SMD]"]
  VCC1 = Battery block 9V

nets:
  N1: Part1.D2, R1.Pin_1
  N2: Part1.GND, VCC1.-
  N3: R1.Pin_0, VCC1.+

notes:
  Liquid flow meter
